# Fritzing sketch schematic (saved by Fritzing 0.9.3b)
breadboards: 1

parts:
  V1 = DC Power [voltage=12V]
  0_1uF = Capacitor [package=cap-pth-large]
  0_33uF = Capacitor [package=cap-pth-large]
  IC1 = Voltage Regulator [package=to-220-alt]
  U1 = attiny85 [package=dip]
  C1 = Electrolytic Capacitor [capacitance=100µF package="200 mil [THT, electrolytic]"]
  Q1 = Basic FET N-Channel [package="TO220 [THT]"]
  R1 = Resistor [tolerance=±5% resistance=10k package="2512 [SMD]"]
  LED1 = LEDs [package=led10mm]
  U2 = POT [package=pot_mammoth]
  R2 = Photocell (LDR) [package=THT]
  R3 = Resistor [tolerance=±5% resistance=10k package="2512 [SMD]"]

nets:
  N1: V1.V+, 0_33uF.1, IC1.IN, LED1.C
  N2: V1.V-, 0_1uF.2, 0_33uF.2, IC1.GND, U1.Pin_4, C1.-, Q1.source, R1.Pin_0, U2.E, R3.Pin_0
  N3: 0_1uF.1, IC1.OUT, U1.Pin_8, C1.+, U2.A, R2.pin_0
  N4: U1.Pin_3, U2.S
  N5: U1.Pin_5, Q1.gate, R1.Pin_1
  N6: U1.Pin_7, R2.pin_1, R3.Pin_1
  N7: Q1.drain, LED1.A
